# Fritzing sketch FritzingProject (saved by Fritzing 0.7.0b)
breadboards: 1

parts:
  Arduino1 = Arduino
  LED1 = LED - 5mm [color="Red (633nm)" package="5 mm [THT]"]
  LED2 = LED - 5mm [color="Red (633nm)" package="5 mm [THT]"]
  LED3 = LED - 5mm [color="Red (633nm)" package="5 mm [THT]"]
  LED4 = LED - 5mm [color="Red (633nm)" package="5 mm [THT]"]
  LED5 = LED - 5mm [color="Red (633nm)" package="5 mm [THT]"]
  LED6 = LED - 5mm [color="Red (633nm)" package="5 mm [THT]"]
  S1 = Pushbutton [package="[THT]"]
  S2 = Pushbutton [package="[THT]"]
  LED7 = RGB LED (com. cathode, rbg) [package="5 mm [THT]"]
  R1 = Resistor [tolerance=±5% resistance=220 package=THT]
  R2 = Resistor [tolerance=±5% resistance=220 package=THT]
  R3 = Resistor [tolerance=±5% resistance=220 package=THT]
  R4 = Resistor [tolerance=±5% resistance=220 package=THT]
  R5 = Resistor [tolerance=±5% resistance=220 package=THT]
  R6 = Resistor [tolerance=±5% resistance=220 package=THT]
  R7 = Resistor [tolerance=±5% resistance=220 package=THT]

nets:
  N1: Arduino1.GND, R1.Pin_1, R2.Pin_1, R3.Pin_1, R4.Pin_1, R5.Pin_1, R6.Pin_1, R7.Pin_1
  N2: Arduino1.D10, LED6.anode
  N3: Arduino1.D9, LED5.anode
  N4: Arduino1.D8, LED4.anode
  N5: Arduino1.D7, LED3.anode
  N6: Arduino1.D6, LED2.anode
  N7: Arduino1.D5, LED1.anode
  N8: Arduino1.D4, LED7.red_anode
  N9: Arduino1.D3, LED7.blue_anode
  N10: Arduino1.D2, LED7.green_anode
  N11: Arduino1.+5V, S1.Pin_1, S1.Pin_2, S2.Pin_1, S2.Pin_2
  N12: Arduino1.A2, S1.Pin_4
  N13: Arduino1.A3, S2.Pin_3, S2.Pin_4
  N14: LED1.cathode, R4.Pin_0
  N15: LED2.cathode, R3.Pin_0
  N16: LED3.cathode, R2.Pin_0
  N17: LED4.cathode, R5.Pin_0
  N18: LED5.cathode, R6.Pin_0
  N19: LED6.cathode, R7.Pin_0
  N20: LED7.common_cathode, R1.Pin_0
